// Digital circuit main.dig as structural Verilog
module main (
  input  Clock,
  output [15:0] Imediato
);

  wire [4:0] multiplexer_1_out;
  wire [5:0] OPCODE;
  wire [25:16] instruction_mem_1__32b__out;
  wire [31:0] _32x32_1_p7, _32x32_1_p8, add_1_s, bitextender_1_out, multiplexer_2_out, pc_1_pc_out,
       ramasync_1_q, ula_1_resultado, WB;

  PC pc_1 (.Clok(Clock), .PC_IN(add_1_s), .PC_OUT(pc_1_pc_out));
  Add #(.Bits(32)) add_1 (.a(pc_1_pc_out), .b(32'h4), .c_i(1'b0), .s(add_1_s));  // open: c_o
  instruction_mem instruction_mem_1 (
    ._32b__ADDR(pc_1_pc_out), ._1b__Enable(Clock), ._32b__Out({OPCODE, instruction_mem_1__32b__out, Imediato}));
  Multiplexer #(.Bits(5)) multiplexer_1 (
    .sel(1'b0), .in_0(instruction_mem_1__32b__out[20:16]), .in_1(Imediato[15:11]), .out(multiplexer_1_out));
  // _32x32 _32x32_1: pin names not known; wires that end beside it: WB, instruction_mem_1__32b__out[25:21], instruction_mem_1__32b__out[20:16], multiplexer_1_out, Clock, 1'b0, _32x32_1_p7, _32x32_1_p8
  BitExtender #(.inputBits(16), .outputBits(32)) bitextender_1 (.in(Imediato), .out(bitextender_1_out));
  Multiplexer #(.Bits(32)) multiplexer_2 (
    .sel(1'b0), .in_0(_32x32_1_p8), .in_1(bitextender_1_out), .out(multiplexer_2_out));
  ula ula_1 (
    .ALUControl(4'b0000), .A(_32x32_1_p7), .B(multiplexer_2_out), .Shamt({6{1'b0}}),
    .Resultado(ula_1_resultado));  // open: Zero
  RAMAsync #(.AddrBits(24), .Bits(32)) ramasync_1 (
    .A(ula_1_resultado[23:0]), .D(_32x32_1_p8), .we(1'b0), .Q(ramasync_1_q));
  Multiplexer #(.Bits(32)) multiplexer_3 (.sel(1'b0), .in_0(ramasync_1_q), .in_1(ula_1_resultado), .out(WB));
endmodule
